// Logisim project hw4.circ as structural Verilog: 4 circuits, main circuit main
module main (
);

  D_Flip_Flop d_ff_1 ();  // open: clk, D, Q, Qn, preset, reset
  ROM Instruction_Memory_b2d019ad ();  // open: addr, data
  RAM Data_Memory_704a74f6 ();  // open: addr, data, sel, clk, ld, clr
endmodule

module RegisterFile (
  input  [2:0] rd,
  input  wr_enable,
  input  [15:0] data_in,
  input  clk,
  input  reset,
  input  [2:0] rs1,
  input  [2:0] rs2,
  output [15:0] rs2_out,
  output [15:0] rs1_out
);

  wire decoder_1_out0, decoder_1_out1, decoder_1_out2, decoder_1_out3, decoder_1_out4, decoder_1_out5,
       decoder_1_out6, decoder_1_out7, decoder_2_out0, decoder_2_out1, decoder_2_out2, decoder_2_out3,
       decoder_2_out4, decoder_2_out5, decoder_2_out6, decoder_2_out7, decoder_3_out0, decoder_3_out1,
       decoder_3_out2, decoder_3_out3, decoder_3_out4, decoder_3_out5, decoder_3_out6, decoder_3_out7;
  wire [15:0] createregister_1_data_out, createregister_2_data_out, createregister_3_data_out,
       createregister_4_data_out, createregister_5_data_out, createregister_6_data_out,
       createregister_7_data_out, createregister_8_data_out;

  Decoder #(.select(3)) decoder_1 (
    .out0(decoder_1_out0), .out1(decoder_1_out1), .out2(decoder_1_out2), .out3(decoder_1_out3),
    .out4(decoder_1_out4), .out5(decoder_1_out5), .out6(decoder_1_out6), .out7(decoder_1_out7), .sel(rd),
    .en(wr_enable));
  CreateRegister createregister_1 (
    .reset(reset), .clk(clk), .write_en(decoder_1_out0), .data_in(data_in),
    .data_out(createregister_1_data_out));
  CreateRegister createregister_2 (
    .reset(reset), .clk(clk), .write_en(decoder_1_out1), .data_in(data_in),
    .data_out(createregister_2_data_out));
  CreateRegister createregister_3 (
    .reset(reset), .clk(clk), .write_en(decoder_1_out2), .data_in(data_in),
    .data_out(createregister_3_data_out));
  CreateRegister createregister_4 (
    .reset(reset), .clk(clk), .write_en(decoder_1_out3), .data_in(data_in),
    .data_out(createregister_4_data_out));
  CreateRegister createregister_5 (
    .reset(reset), .clk(clk), .write_en(decoder_1_out4), .data_in(data_in),
    .data_out(createregister_5_data_out));
  CreateRegister createregister_6 (
    .reset(reset), .clk(clk), .write_en(decoder_1_out5), .data_in(data_in),
    .data_out(createregister_6_data_out));
  CreateRegister createregister_7 (
    .reset(reset), .clk(clk), .write_en(decoder_1_out6), .data_in(data_in),
    .data_out(createregister_7_data_out));
  CreateRegister createregister_8 (
    .reset(reset), .clk(clk), .write_en(decoder_1_out7), .data_in(data_in),
    .data_out(createregister_8_data_out));
  Decoder #(.select(3)) decoder_2 (
    .out0(decoder_2_out0), .out1(decoder_2_out1), .out2(decoder_2_out2), .out3(decoder_2_out3),
    .out4(decoder_2_out4), .out5(decoder_2_out5), .out6(decoder_2_out6), .out7(decoder_2_out7), .sel(rs1));  // open: en
  assign rs1_out = decoder_2_out2 ? createregister_3_data_out : 16'bz;  // Controlled_Buffer controlled_buffer_1
  assign rs1_out = decoder_2_out1 ? createregister_2_data_out : 16'bz;  // Controlled_Buffer controlled_buffer_2
  assign rs1_out = decoder_2_out0 ? createregister_1_data_out : 16'bz;  // Controlled_Buffer controlled_buffer_3
  assign rs1_out = decoder_2_out6 ? createregister_7_data_out : 16'bz;  // Controlled_Buffer controlled_buffer_4
  assign rs1_out = decoder_2_out5 ? createregister_6_data_out : 16'bz;  // Controlled_Buffer controlled_buffer_5
  assign rs1_out = decoder_2_out4 ? createregister_5_data_out : 16'bz;  // Controlled_Buffer controlled_buffer_6
  assign rs1_out = decoder_2_out3 ? createregister_4_data_out : 16'bz;  // Controlled_Buffer controlled_buffer_7
  assign rs2_out = decoder_3_out2 ? createregister_3_data_out : 16'bz;  // Controlled_Buffer controlled_buffer_8
  assign rs2_out = decoder_3_out1 ? createregister_2_data_out : 16'bz;  // Controlled_Buffer controlled_buffer_9
  assign rs2_out = decoder_3_out0 ? createregister_1_data_out : 16'bz;  // Controlled_Buffer controlled_buffer_10
  assign rs1_out = decoder_2_out7 ? createregister_8_data_out : 16'bz;  // Controlled_Buffer controlled_buffer_11
  Decoder #(.select(3)) decoder_3 (
    .out0(decoder_3_out0), .out1(decoder_3_out1), .out2(decoder_3_out2), .out3(decoder_3_out3),
    .out4(decoder_3_out4), .out5(decoder_3_out5), .out6(decoder_3_out6), .out7(decoder_3_out7), .sel(rs2));  // open: en
  assign rs2_out = decoder_3_out6 ? createregister_7_data_out : 16'bz;  // Controlled_Buffer controlled_buffer_12
  assign rs2_out = decoder_3_out5 ? createregister_6_data_out : 16'bz;  // Controlled_Buffer controlled_buffer_13
  assign rs2_out = decoder_3_out4 ? createregister_5_data_out : 16'bz;  // Controlled_Buffer controlled_buffer_14
  assign rs2_out = decoder_3_out3 ? createregister_4_data_out : 16'bz;  // Controlled_Buffer controlled_buffer_15
  assign rs2_out = decoder_3_out7 ? createregister_8_data_out : 16'bz;  // Controlled_Buffer controlled_buffer_16
endmodule

module CreateRegister (
  input  reset,
  input  clk,
  input  write_en,
  input  [15:0] data_in,
  output [15:0] data_out
);

  wire and_1_out;

  and and_1 (and_1_out, clk, write_en);
  D_Flip_Flop d_ff_1 (.D(data_in[0]), .clk(and_1_out), .Q(data_out[0]), .reset(reset));  // open: Qn, preset
  D_Flip_Flop d_ff_2 (.D(data_in[1]), .clk(and_1_out), .Q(data_out[1]), .reset(reset));  // open: Qn, preset
  D_Flip_Flop d_ff_3 (.D(data_in[2]), .clk(and_1_out), .Q(data_out[2]), .reset(reset));  // open: Qn, preset
  D_Flip_Flop d_ff_4 (.D(data_in[3]), .clk(and_1_out), .Q(data_out[3]), .reset(reset));  // open: Qn, preset
  D_Flip_Flop d_ff_5 (.D(data_in[4]), .clk(and_1_out), .Q(data_out[4]), .reset(reset));  // open: Qn, preset
  D_Flip_Flop d_ff_6 (.D(data_in[5]), .clk(and_1_out), .Q(data_out[5]), .reset(reset));  // open: Qn, preset
  D_Flip_Flop d_ff_7 (.D(data_in[6]), .clk(and_1_out), .Q(data_out[6]), .reset(reset));  // open: Qn, preset
  D_Flip_Flop d_ff_8 (.D(data_in[7]), .clk(and_1_out), .Q(data_out[7]), .reset(reset));  // open: Qn, preset
  D_Flip_Flop d_ff_9 (.D(data_in[8]), .clk(and_1_out), .Q(data_out[8]), .reset(reset));  // open: Qn, preset
  D_Flip_Flop d_ff_10 (.D(data_in[9]), .clk(and_1_out), .Q(data_out[9]), .reset(reset));  // open: Qn, preset
  D_Flip_Flop d_ff_11 (.D(data_in[10]), .clk(and_1_out), .Q(data_out[10]), .reset(reset));  // open: Qn, preset
  D_Flip_Flop d_ff_12 (.D(data_in[11]), .clk(and_1_out), .Q(data_out[11]), .reset(reset));  // open: Qn, preset
  D_Flip_Flop d_ff_13 (.D(data_in[12]), .clk(and_1_out), .Q(data_out[12]), .reset(reset));  // open: Qn, preset
  D_Flip_Flop d_ff_14 (.D(data_in[13]), .clk(and_1_out), .Q(data_out[13]), .reset(reset));  // open: Qn, preset
  D_Flip_Flop d_ff_15 (.D(data_in[14]), .clk(and_1_out), .Q(data_out[14]), .reset(reset));  // open: Qn, preset
  D_Flip_Flop d_ff_16 (.D(data_in[15]), .clk(and_1_out), .Q(data_out[15]), .reset(reset));  // open: Qn, preset

  // Notes on the sheet:
  //   clk: pull=up
endmodule

module MemoryLatch (
  input  [15:0] address,
  input  WE,
  input  clk,
  input  [15:0] data_in,
  output [15:0] address_latched,
  output WE_latched,
  output OE_latched,
  output [15:0] data_in_latched
);

  wire d_ff_1_q;
  wire [15:0] register_1_q;

  Register #(.width(16), .trigger("falling")) register_1 (
    .D(address), .en(WE), .clk(clk), .Q(register_1_q));  // open: clr
  Register #(.width(16), .trigger("falling")) register_2 (
    .D(data_in), .en(WE), .clk(clk), .Q(data_in_latched));  // open: clr
  D_Flip_Flop #(.trigger("falling")) d_ff_1 (.D(WE), .clk(clk), .Q(d_ff_1_q));  // open: Qn, preset, reset
  Multiplexer #(.width(16), .enable("false")) multiplexer_1 (
    .in0(address), .in1(register_1_q), .out(address_latched), .sel(d_ff_1_q));
  and and_1 (WE_latched, clk, d_ff_1_q);
  not not_1 (OE_latched, WE_latched);
endmodule
